// Logisim project Lab 1_Function Implement in Circuit.circ as structural Verilog: 4 circuits, main circuit main
module main (
  input  A,
  input  B,
  input  C,
  output out_4
);

  wire ic_7404_1_out_10, ic_7404_1_out_12, ic_7408_1_out_9, ic_7408_1_out_11, ic_7408_1_out_12,
       ic_7432_1_out_10;

  IC_7404 ic_7404_1 (
    .in_4(A), .in_6(B), .out_10(ic_7404_1_out_10), .out_12(ic_7404_1_out_12));  // open: in_1, in_2, in_3, in_5, out_7, out_8, out_9, out_11
  IC_7432 ic_7432_1 (
    .in_3(ic_7408_1_out_11), .in_4(ic_7408_1_out_9), .in_5(ic_7408_1_out_12), .in_6(ic_7432_1_out_10),
    .out_10(ic_7432_1_out_10), .out_11(out_4));  // open: in_1, in_2, in_7, in_8, out_9, out_12
  IC_7408 ic_7408_1 (
    .in_1(ic_7404_1_out_12), .in_2(A), .in_5(C), .in_6(ic_7404_1_out_10), .in_7(B), .in_8(C),
    .out_9(ic_7408_1_out_9), .out_11(ic_7408_1_out_11), .out_12(ic_7408_1_out_12));  // open: in_3, in_4, out_10

  // Notes on the sheet:
  //   A'
  //   B'
  //   F = A'C + AB' + BC
  //   C
  //   BC
  //   A'C + AB' 
  //   A'
  //   C
  //   C
  //   B
  //   BC
  //   A'C
  //   AB'
  //   A'C
  //   AB'
  //   A
  //   B'
  //   A'C + AB' 
endmodule

module IC_7408 (
  input  in_1,
  input  in_2,
  input  in_3,
  input  in_4,
  input  in_5,
  input  in_6,
  input  in_7,
  input  in_8,
  output out_9,
  output out_10,
  output out_11,
  output out_12
);

  and and_1 (out_9, in_1, in_2);
  and and_2 (out_10, in_3, in_4);
  and and_3 (out_11, in_5, in_6);
  and and_4 (out_12, in_7, in_8);
endmodule

module IC_7432 (
  input  in_1,
  input  in_2,
  input  in_3,
  input  in_4,
  input  in_5,
  input  in_6,
  input  in_7,
  input  in_8,
  output out_9,
  output out_10,
  output out_11,
  output out_12
);

  or or_1 (out_9, in_1, in_2);
  or or_2 (out_10, in_3, in_4);
  or or_3 (out_11, in_5, in_6);
  or or_4 (out_12, in_7, in_8);
endmodule

module IC_7404 (
  input  in_1,
  input  in_2,
  input  in_3,
  input  in_4,
  input  in_5,
  input  in_6,
  output out_7,
  output out_8,
  output out_9,
  output out_10,
  output out_11,
  output out_12
);

  not not_1 (out_7, in_1);
  not not_2 (out_8, in_2);
  not not_3 (out_9, in_3);
  not not_4 (out_10, in_4);
  not not_5 (out_11, in_5);
  not not_6 (out_12, in_6);
endmodule
