// Logisim project Lab 2_Basic gates using NAND gates.circ as structural Verilog: 2 circuits, main circuit main
module main (
  input  A,
  input  B,
  output NOT_using_NAND,
  output AB,
  output out_5
);

  wire ic_7400_1_out_12, ic_7400_2_out_11, ic_7400_2_out_12;

  IC_7400 ic_7400_1 (
    .in_1(ic_7400_1_out_12), .in_2(ic_7400_1_out_12), .in_5(A), .in_6(A), .in_7(B), .in_8(A), .out_9(AB),
    .out_11(NOT_using_NAND), .out_12(ic_7400_1_out_12));  // open: in_3, in_4, out_10
  IC_7400 ic_7400_2 (
    .in_3(ic_7400_2_out_12), .in_4(ic_7400_2_out_11), .in_5(A), .in_6(A), .in_7(B), .in_8(B), .out_10(out_5),
    .out_11(ic_7400_2_out_11), .out_12(ic_7400_2_out_12));  // open: in_1, in_2, out_9

  // Notes on the sheet:
  //   A
  //   A
  //   B
  //   A
  //   B
  //   (AB)'
  //   A'
  //   B'
  //   B'
  //   (AB)'
  //   A'
  //   A'
  //   A + B
  //   AND using NAND
  //   OR using NAND
endmodule

module IC_7400 (
  input  in_1,
  input  in_2,
  input  in_3,
  input  in_4,
  input  in_5,
  input  in_6,
  input  in_7,
  input  in_8,
  output out_9,
  output out_10,
  output out_11,
  output out_12
);

  nand nand_1 (out_9, in_1, in_2);
  nand nand_2 (out_10, in_3, in_4);
  nand nand_3 (out_11, in_5, in_6);
  nand nand_4 (out_12, in_7, in_8);
endmodule
