// Logisim project Lab 2_Basic gates using NOR gates.circ as structural Verilog: 2 circuits, main circuit main
module main (
  input  A,
  input  B,
  output F___A_prime,
  output F___AB,
  output F___A_B
);

  wire A_out_10, A_out_12, ic_7402_1_out_11;

  IC_7402 u_A (
    .in_1(A_out_10), .in_2(A_out_12), .in_3(A), .in_4(A), .in_5(A), .in_6(A), .in_7(B), .in_8(B),
    .out_9(F___AB), .out_10(A_out_10), .out_11(F___A_prime), .out_12(A_out_12));
  IC_7402 ic_7402_1 (
    .in_5(A), .in_6(B), .in_7(ic_7402_1_out_11), .in_8(ic_7402_1_out_11), .out_11(ic_7402_1_out_11),
    .out_12(F___A_B));  // open: in_1, in_2, in_3, in_4, out_9, out_10

  // Notes on the sheet:
  //   NOT using NOR
  //   A
  //   B
  //   B'
  //   A
  //   B
  //   (A+B)'
  //   A
  //   A'
  //   B'
  //   AND gate using NOR gate
  //   OR gate using NOR gate
endmodule

module IC_7402 (
  input  in_1,
  input  in_2,
  input  in_3,
  input  in_4,
  input  in_5,
  input  in_6,
  input  in_7,
  input  in_8,
  output out_9,
  output out_10,
  output out_11,
  output out_12
);

  nor nor_1 (out_9, in_1, in_2);
  nor nor_2 (out_10, in_3, in_4);
  nor nor_3 (out_11, in_5, in_6);
  nor nor_4 (out_12, in_7, in_8);
endmodule
