// Logisim project Lab 2_Figure D2_using NAND gates(minimized).circ as structural Verilog: 2 circuits, main circuit main
module main (
  input  A,
  input  B,
  input  C,
  output F____AC___BC_prime
);

  wire ic_7400_1_out_9, ic_7400_1_out_11, ic_7400_1_out_12;

  IC_7400 ic_7400_1 (
    .in_1(ic_7400_1_out_12), .in_2(B), .in_3(ic_7400_1_out_9), .in_4(ic_7400_1_out_11), .in_5(A), .in_6(C),
    .in_7(C), .in_8(C), .out_9(ic_7400_1_out_9), .out_10(F____AC___BC_prime), .out_11(ic_7400_1_out_11),
    .out_12(ic_7400_1_out_12));

  // Notes on the sheet:
  //   (AC)'
  //   C'
  //   C'
  //   (AC)'
  //   (BC')'
  //   C'
  //   (BC')'
endmodule

module IC_7400 (
  input  in_1,
  input  in_2,
  input  in_3,
  input  in_4,
  input  in_5,
  input  in_6,
  input  in_7,
  input  in_8,
  output out_9,
  output out_10,
  output out_11,
  output out_12
);

  nand nand_1 (out_9, in_1, in_2);
  nand nand_2 (out_10, in_3, in_4);
  nand nand_3 (out_11, in_5, in_6);
  nand nand_4 (out_12, in_7, in_8);
endmodule
