// Logisim project Lab 2_XOR using NAND.circ as structural Verilog: 2 circuits, main circuit main
module main (
  input  A,
  input  B,
  output F___A_prime_B___AB_prime
);

  wire ic_7400_1_out_9, ic_7400_1_out_10, ic_7400_1_out_11;

  IC_7400 ic_7400_1 (
    .in_1(B), .in_2(ic_7400_1_out_11), .in_3(A), .in_4(ic_7400_1_out_11), .in_5(A), .in_6(B),
    .in_7(ic_7400_1_out_10), .in_8(ic_7400_1_out_9), .out_9(ic_7400_1_out_9), .out_10(ic_7400_1_out_10),
    .out_11(ic_7400_1_out_11), .out_12(F___A_prime_B___AB_prime));

  // Notes on the sheet:
  //   (AB)'
  //   (AB)'
  //   B
  //   XOR
  //   A' + AB
  //   B' + AB
endmodule

module IC_7400 (
  input  in_1,
  input  in_2,
  input  in_3,
  input  in_4,
  input  in_5,
  input  in_6,
  input  in_7,
  input  in_8,
  output out_9,
  output out_10,
  output out_11,
  output out_12
);

  nand nand_1 (out_9, in_1, in_2);
  nand nand_2 (out_10, in_3, in_4);
  nand nand_3 (out_11, in_5, in_6);
  nand nand_4 (out_12, in_7, in_8);
endmodule
