// Logisim project Lab 5_Experiment 1.circ as structural Verilog: 2 circuits, main circuit main
module main (
  input  M,
  input  B3,
  input  B2,
  input  B1,
  input  B0,
  input  A3,
  input  A2,
  input  A1,
  input  A0,
  output out_10,
  output C,
  output S4,
  output S3,
  output S2,
  output S1
);

  IC_74283 ic_74283_1 (
    .M(M), .S4(S4), .C4(C), .B3(B3), .A3(A3), .B2(B2), .A2(A2), .B1(B1), .A1(A1), .B0(B0), .A0(A0), .S3(S3),
    .S2(S2), .S1(S1));
endmodule

module IC_74283 (
  input  M,
  input  A3,
  input  A2,
  input  A1,
  input  A0,
  input  B3,
  input  B2,
  input  B1,
  input  B0,
  output S3,
  output S2,
  output S1,
  output S4,
  output C4
);

  wire adder_1_cout, adder_2_cout, adder_3_cout, xor_1_out, xor_2_out, xor_3_out, xor_4_out;

  xor xor_1 (xor_1_out, B1, M);
  xor xor_2 (xor_2_out, B3, M);
  xor xor_3 (xor_3_out, B0, M);
  xor xor_4 (xor_4_out, B2, M);
  Adder #(.width(1)) adder_1 (.a(A0), .b(xor_3_out), .out(S1), .cin(M), .cout(adder_1_cout));
  Adder #(.width(1)) adder_2 (.a(A1), .b(xor_1_out), .out(S2), .cin(adder_1_cout), .cout(adder_2_cout));
  Adder #(.width(1)) adder_3 (.a(A2), .b(xor_4_out), .out(S3), .cin(adder_2_cout), .cout(adder_3_cout));
  Adder #(.width(1)) adder_4 (.a(A3), .b(xor_2_out), .out(S4), .cin(adder_3_cout), .cout(C4));
endmodule
