// Logisim project Lab 5_Experiment 2.circ as structural Verilog: 4 circuits, main circuit main
module main (
  input  M,
  input  A4,
  input  A3,
  input  A2,
  input  A1,
  input  B4,
  input  B3,
  input  B2,
  input  B1,
  output C,
  output Cout,
  output S4,
  output S3,
  output S2,
  output S1
);

  wire ic_7408_1_out_11, ic_7408_1_out_12, ic_7432_1_out_9, ic_74283_1_c4, ic_74283_1_s1, ic_74283_1_s2,
       ic_74283_1_s3, ic_74283_1_s4;

  IC_74283 ic_74283_1 (
    .M(M), .S4(ic_74283_1_s4), .C4(ic_74283_1_c4), .B3(A4), .A3(B4), .B2(A3), .A2(B3), .B1(A2), .A1(B2),
    .B0(A1), .A0(B1), .S3(ic_74283_1_s3), .S2(ic_74283_1_s2), .S1(ic_74283_1_s1));
  IC_74283 ic_74283_2 (
    .M(M), .S4(S4), .C4(Cout), .B3(M), .A3(ic_74283_1_s4), .B2(C), .A2(ic_74283_1_s3), .B1(C),
    .A1(ic_74283_1_s2), .B0(M), .A0(ic_74283_1_s1), .S3(S3), .S2(S2), .S1(S1));
  IC_7432 ic_7432_1 (
    .in_1(ic_7408_1_out_11), .in_2(ic_7408_1_out_12), .in_3(ic_74283_1_c4), .in_4(ic_7432_1_out_9),
    .out_9(ic_7432_1_out_9), .out_10(C));  // open: in_5, in_6, in_7, in_8, out_11, out_12
  IC_7408 ic_7408_1 (
    .in_5(ic_74283_1_s4), .in_6(ic_74283_1_s3), .in_7(ic_74283_1_s4), .in_8(ic_74283_1_s2),
    .out_11(ic_7408_1_out_11), .out_12(ic_7408_1_out_12));  // open: in_1, in_2, in_3, in_4, out_9, out_10

  // Notes on the sheet:
  //   Ignored
  //   BCD Carry
endmodule

module IC_7408 (
  input  in_1,
  input  in_2,
  input  in_3,
  input  in_4,
  input  in_5,
  input  in_6,
  input  in_7,
  input  in_8,
  output out_9,
  output out_10,
  output out_11,
  output out_12
);

  and and_1 (out_9, in_1, in_2);
  and and_2 (out_10, in_3, in_4);
  and and_3 (out_11, in_5, in_6);
  and and_4 (out_12, in_7, in_8);
endmodule

module IC_7432 (
  input  in_1,
  input  in_2,
  input  in_3,
  input  in_4,
  input  in_5,
  input  in_6,
  input  in_7,
  input  in_8,
  output out_9,
  output out_10,
  output out_11,
  output out_12
);

  or or_1 (out_9, in_1, in_2);
  or or_2 (out_10, in_3, in_4);
  or or_3 (out_11, in_5, in_6);
  or or_4 (out_12, in_7, in_8);
endmodule

module IC_74283 (
  input  M,
  input  A3,
  input  A2,
  input  A1,
  input  A0,
  input  B3,
  input  B2,
  input  B1,
  input  B0,
  output S3,
  output S2,
  output S1,
  output S4,
  output C4
);

  wire adder_1_cout, adder_2_cout, adder_3_cout, xor_1_out, xor_2_out, xor_3_out, xor_4_out;

  xor xor_1 (xor_1_out, B1, M);
  xor xor_2 (xor_2_out, B3, M);
  xor xor_3 (xor_3_out, B0, M);
  xor xor_4 (xor_4_out, B2, M);
  Adder #(.width(1)) adder_1 (.a(A0), .b(xor_3_out), .out(S1), .cin(M), .cout(adder_1_cout));
  Adder #(.width(1)) adder_2 (.a(A1), .b(xor_1_out), .out(S2), .cin(adder_1_cout), .cout(adder_2_cout));
  Adder #(.width(1)) adder_3 (.a(A2), .b(xor_4_out), .out(S3), .cin(adder_2_cout), .cout(adder_3_cout));
  Adder #(.width(1)) adder_4 (.a(A3), .b(xor_2_out), .out(S4), .cin(adder_3_cout), .cout(C4));
endmodule
