// Logisim project Lab 6_Task 1_ 4 to 1 mux with enable pin.circ as structural Verilog: 2 circuits, main circuit main
module main (
  input  I3,
  input  I2,
  input  I1,
  input  I0,
  input  in_5,
  input  S1,
  input  En,
  output out_8,
  output F
);

  _4_1_MAX u_4_1_max_1 (.I0(I0), .I1(I1), .I2(I2), .I3(I3), .out_8(F), .S0(in_5), .S1(S1), .En(En));

  // Notes on the sheet:
  //   S0
  //   Figure: 4:1 mux with enable pin
endmodule

module _4_1_MAX (
  input  I0,
  input  I1,
  input  I2,
  input  I3,
  input  S0,
  input  S1,
  input  En,
  output out_8
);

  wire and_1_out, and_2_out, and_3_out, and_4_out, not_1_out, not_2_out;

  not not_1 (not_1_out, S0);
  not not_2 (not_2_out, S1);
  and and_1 (and_1_out, I0, not_2_out, not_1_out, En);
  and and_2 (and_2_out, I1, not_2_out, S0, En);
  and and_3 (and_3_out, I2, S1, not_1_out, En);
  and and_4 (and_4_out, I3, S1, S0, En);
  or or_1 (out_8, and_1_out, and_2_out, and_3_out, and_4_out);

  // Notes on the sheet:
  //   Figure: 4:1 mux with enable pin
endmodule
