// Logisim project Lab 6_Task 2_Function implementation using 8 to 1 mux.circ as structural Verilog: 2 circuits, main circuit main
module main (
  input  D,
  input  A,
  input  B,
  input  C,
  input  in_5,
  output F
);

  Multiplexer #(.select(3), .enable("false")) multiplexer_1 (
    .in0(1'b1), .in1(D), .in2(D), .in3(in_5), .in4(1'b1), .in5(in_5), .in6(in_5), .in7(1'b1), .out(F),
    .sel({A, B, C}));

  // Notes on the sheet:
  //   Figure: Table F.2.1 using 8:1 mux
endmodule

module IC_74151 (
  input  I0,
  input  I1,
  input  I2,
  input  I3,
  input  I4,
  input  I5,
  input  I6,
  input  I7,
  input  S2,
  input  S1,
  input  S0,
  output out_12
);

  Multiplexer #(.select(3), .enable("false")) multiplexer_1 (
    .in0(I0), .in1(I1), .in2(I2), .in3(I3), .in4(I4), .in5(I5), .in6(I6), .in7(I7), .out(out_12),
    .sel({S2, S1, S0}));
endmodule
