// Logisim project Lab 6_Task 3_ 3 to 8 line decoder.circ as structural Verilog: 2 circuits, main circuit main
module main (
  input  [2:0] Input_pins,
  output Y0,
  output Y1,
  output Y2,
  output Y3,
  output Y4,
  output Y5,
  output Y6,
  output Y7,
  output out_10
);

  wire decoder_1_out0, decoder_1_out1, decoder_1_out2, decoder_1_out3, decoder_1_out4, decoder_1_out5,
       decoder_1_out6, decoder_1_out7;

  Decoder #(.select(3), .enable("false")) decoder_1 (
    .out0(decoder_1_out0), .out1(decoder_1_out1), .out2(decoder_1_out2), .out3(decoder_1_out3),
    .out4(decoder_1_out4), .out5(decoder_1_out5), .out6(decoder_1_out6), .out7(decoder_1_out7),
    .sel(Input_pins));
  IC_7404 ic_7404_1 (
    .in_1(decoder_1_out3), .in_2(decoder_1_out4), .in_3(decoder_1_out5), .in_4(decoder_1_out0),
    .in_5(decoder_1_out1), .in_6(decoder_1_out2), .out_7(Y3), .out_8(Y4), .out_9(Y5), .out_10(Y0),
    .out_11(Y1), .out_12(Y2));
  IC_7404 ic_7404_2 (
    .in_4(decoder_1_out6), .in_5(decoder_1_out7), .out_10(Y6), .out_11(Y7));  // open: in_1, in_2, in_3, in_6, out_7, out_8, out_9, out_12

  // Notes on the sheet:
  //   (C,B,A)
  //   Figure: 3 to 8 line Decoder
endmodule

module IC_7404 (
  input  in_1,
  input  in_2,
  input  in_3,
  input  in_4,
  input  in_5,
  input  in_6,
  output out_7,
  output out_8,
  output out_9,
  output out_10,
  output out_11,
  output out_12
);

  not not_1 (out_7, in_1);
  not not_2 (out_8, in_2);
  not not_3 (out_9, in_3);
  not not_4 (out_10, in_4);
  not not_5 (out_11, in_5);
  not not_6 (out_12, in_6);
endmodule
