// Logisim project lab 8_Counter using T-flip flop.circ as structural Verilog: 9 circuits, main circuit main
module main (
  input  X,
  input  Reset,
  input  Enable,
  input  Reset_2
);

  wire and_1_out, and_2_out, and_3_out, and_4_out, clock_1_out, not_1_out, or_1_out, t_ff_1_q, t_ff_1_qn,
       t_ff_2_q, t_ff_2_qn;

  not not_1 (not_1_out, X);
  and and_1 (and_1_out, t_ff_1_qn, X, t_ff_2_qn);
  and and_2 (and_2_out, t_ff_1_qn, not_1_out, t_ff_2_q);
  and and_3 (and_3_out, t_ff_1_q, X, t_ff_2_q);
  and and_4 (and_4_out, t_ff_1_q, not_1_out, t_ff_2_qn);
  or or_1 (or_1_out, and_1_out, and_2_out, and_3_out, and_4_out);
  Clock clock_1 (.out(clock_1_out));
  T_Flip_Flop t_ff_1 (
    .clk(clock_1_out), .T(or_1_out), .Q(t_ff_1_q), .Qn(t_ff_1_qn), .reset(Reset), .en(Enable));  // open: preset
  T_Flip_Flop t_ff_2 (
    .clk(clock_1_out), .T(1'b1), .Q(t_ff_2_q), .Qn(t_ff_2_qn), .reset(Reset_2), .en(Enable));  // open: preset

  // Notes on the sheet:
  //   A'B'X
  //   A'BX'
  //   ABX
  //   AB'X'
  //   A
  //   A'
  //   B
  //   B'
endmodule

module IC_7411 (
  input  in_1,
  input  in_2,
  input  in_3,
  input  in_4,
  input  in_5,
  input  in_6,
  input  in_7,
  input  in_8,
  input  in_9,
  output out_10,
  output out_11,
  output out_12
);

  and and_1 (out_10, in_1, in_2, in_3);
  and and_2 (out_11, in_4, in_5, in_6);
  and and_3 (out_12, in_7, in_8, in_9);
endmodule

module IC_4075 (
  input  in_1,
  input  in_2,
  input  in_3,
  input  in_4,
  input  in_5,
  input  in_6,
  input  in_7,
  input  in_8,
  input  in_9,
  output out_10,
  output out_11,
  output out_12
);

  or or_1 (out_10, in_1, in_2, in_3);
  or or_2 (out_11, in_4, in_5, in_6);
  or or_3 (out_12, in_7, in_8, in_9);
endmodule

module IC_7404 (
  input  in_1,
  input  in_2,
  input  in_3,
  input  in_4,
  input  in_5,
  input  in_6,
  output out_7,
  output out_8,
  output out_9,
  output out_10,
  output out_11,
  output out_12
);

  not not_1 (out_7, in_1);
  not not_2 (out_8, in_2);
  not not_3 (out_9, in_3);
  not not_4 (out_10, in_4);
  not not_5 (out_11, in_5);
  not not_6 (out_12, in_6);
endmodule

module IC_7408 (
  input  in_1,
  input  in_2,
  input  in_3,
  input  in_4,
  input  in_5,
  input  in_6,
  input  in_7,
  input  in_8,
  output out_9,
  output out_10,
  output out_11,
  output out_12
);

  and and_1 (out_9, in_1, in_2);
  and and_2 (out_10, in_3, in_4);
  and and_3 (out_11, in_5, in_6);
  and and_4 (out_12, in_7, in_8);
endmodule

module IC_7432 (
  input  in_1,
  input  in_2,
  input  in_3,
  input  in_4,
  input  in_5,
  input  in_6,
  input  in_7,
  input  in_8,
  output out_9,
  output out_10,
  output out_11,
  output out_12
);

  or or_1 (out_9, in_1, in_2);
  or or_2 (out_10, in_3, in_4);
  or or_3 (out_11, in_5, in_6);
  or or_4 (out_12, in_7, in_8);
endmodule

module IC_7400 (
  input  in_1,
  input  in_2,
  input  in_3,
  input  in_4,
  input  in_5,
  input  in_6,
  input  in_7,
  input  in_8,
  output out_9,
  output out_10,
  output out_11,
  output out_12
);

  nand nand_1 (out_9, in_1, in_2);
  nand nand_2 (out_10, in_3, in_4);
  nand nand_3 (out_11, in_5, in_6);
  nand nand_4 (out_12, in_7, in_8);
endmodule

module IC_7402 (
  input  in_1,
  input  in_2,
  input  in_3,
  input  in_4,
  input  in_5,
  input  in_6,
  input  in_7,
  input  in_8,
  output out_9,
  output out_10,
  output out_11,
  output out_12
);

  nor nor_1 (out_9, in_1, in_2);
  nor nor_2 (out_10, in_3, in_4);
  nor nor_3 (out_11, in_5, in_6);
  nor nor_4 (out_12, in_7, in_8);
endmodule

module IC_74151 (
  input  I0,
  input  I1,
  input  I2,
  input  I3,
  input  I4,
  input  I5,
  input  I6,
  input  I7,
  input  S2,
  input  S1,
  input  S0,
  output out_12
);

  Multiplexer #(.select(3), .enable("false")) multiplexer_1 (
    .in0(I0), .in1(I1), .in2(I2), .in3(I3), .in4(I4), .in5(I5), .in6(I6), .in7(I7), .out(out_12),
    .sel({S2, S1, S0}));
endmodule
